# Fritzing sketch Bubba New (saved by Fritzing 0.9.3b)
breadboards: 1

parts:
  U1 = LM 358 Dual Op-Amp [package="DIP8 [THT]"]
  R1 = Resistor [tolerance=±5% resistance=1M package=THT]
  R2 = Resistor [tolerance=±5% resistance=10k package=THT]
  R3 = Resistor [tolerance=±5% resistance=10k package=THT]
  R4 = Resistor [tolerance=±5% resistance=10k package=THT]
  C1 = Ceramic Capacitor [capacitance=100nF package="100 mil [THT, multilayer]"]
  R5 = Resistor [tolerance=±5% resistance=10k package=THT]
  C3 = Ceramic Capacitor [capacitance=100nF package="100 mil [THT, multilayer]"]
  U2 = LM 358 Dual Op-Amp [package="DIP8 [THT]"]
  R6 = Resistor [tolerance=±5% resistance=10k package=THT]
  C4 = Ceramic Capacitor [capacitance=100nF package="100 mil [THT, multilayer]"]
  R7 = Resistor [tolerance=±5% resistance=10k package=THT]
  C5 = Ceramic Capacitor [capacitance=100nF package="100 mil [THT, multilayer]"]
  R8 = Resistor [tolerance=±5% resistance=68k package=THT]

nets:
  N1: U1.connector0, R1.Pin_0, R4.Pin_0
  N2: U1.connector1, R1.Pin_1, R8.Pin_1
  N3: U1.connector2, R2.Pin_0, R3.Pin_1
  GND: U1.connector3, R3.Pin_0, C1.1, C3.1, U2.connector3, C4.1, C5.1
  N4: U1.connector4, R4.Pin_1, C1.0
  N5: U1.connector5, U1.connector6, R5.Pin_1
  5V: U1.connector7, R2.Pin_1, U2.connector7
  N6: R5.Pin_0, C3.0, U2.connector2
  N7: U2.connector0, U2.connector1, R6.Pin_0
  N8: U2.connector4, R6.Pin_1, C4.0
  N9: U2.connector5, U2.connector6, R7.Pin_1
  N10: R7.Pin_0, C5.0, R8.Pin_0
